// Logisim project Module_2_7_15.circ as structural Verilog
module Module2 (
  input  [9:0] Frac,
  input  [4:0] Exp,
  input  Direction,
  output [10:0] Mantissa
);

  wire nor_1_out;

  nor nor_1 (nor_1_out, Exp[0], Exp[1], Exp[2], Exp[3], Exp[4]);
  Multiplexer #(.enable("false")) multiplexer_1 (.in0(1'b1), .in1(1'b0), .out(Mantissa[10]), .sel(nor_1_out));

  assign Mantissa[9:0] = Frac;
endmodule

module Module2_Alternate (
  input  [9:0] Frac,
  input  [4:0] Exp,
  output [10:0] Mantissa
);

  or or_1 (Mantissa[10], Exp[0], Exp[1], Exp[2], Exp[3], Exp[4]);

  assign Mantissa[9:0] = Frac;
endmodule

module Module15 (
  input  [9:0] Frac,
  input  [4:0] Exp,
  input  Sign,
  input  isZero,
  input  Overflow_In,
  input  Underflow_In,
  output [15:0] SUM,
  output Overflow,
  output Underflow
);

  Multiplexer #(.width(16), .enable("false")) multiplexer_1 (
    .in0({Sign, Exp, Frac}), .in1({16{1'b0}}), .out(SUM), .sel(isZero));

  assign Overflow = Overflow_In;
  assign Underflow = Underflow_In;
endmodule

module Module7 (
  input  EA_GT_EB_module3,
  input  EA_EQ_EB_module3,
  input  [10:0] Mantissa_A,
  input  [10:0] Mantissa_B,
  output A_GT_B
);

  wire and_1_out, comparator_1_gt;

  Comparator #(.width(11), .mode("unsigned")) comparator_1 (
    .a(Mantissa_A), .b(Mantissa_B), .gt(comparator_1_gt));  // open: eq, lt
  or or_1 (A_GT_B, EA_GT_EB_module3, and_1_out);
  and and_1 (and_1_out, EA_EQ_EB_module3, comparator_1_gt);
endmodule
